# Fritzing sketch dht with servo (saved by Fritzing 0.9.2b)
breadboards: 1

parts:
  Part1 = Arduino Uno (Rev3)
  DHT-11 = DHT11 Humitidy and Temperature Sensor
  J1 = Basic Servo
  part = Resistor [tolerance=±5% resistance=10k package=THT]

nets:
  N1: Part1.D2, DHT-11.DATA, part.Pin_1
  N2: Part1.D3_PWM, J1.pulse
  5V: Part1.5V, DHT-11.VDD, J1.vcc, part.Pin_0
  GND: Part1.GND, DHT-11.GND, J1.gnd

custom parts:
  DHT11 Humitidy and Temperature Sensor: DHT11 Humidity and Temperature Sensor
